# Fritzing sketch wiring-plan (saved by Fritzing 0.9.4)
breadboards: 1

parts:
  U2 = ESP32S-HiLetgo [part_number=ESP32S-HiLetgo]
  R1 = Resistor [tolerance=±5% resistance=100 package="1206 [SMD]"]
  Q1 = LTR-301 [part_number=LAOMAO-A0056 package=ltr-301]
  IR1 = TSOP312.., 314.. [part_number=VS1838B package=THT]
  Q2 = NPN-Transistor [package="TO92 [THT]"]

nets:
  N1: U2.3.3, IR1.Vs
  N2: U2.GPIO26, IR1.Data
  GND: U2.GND, IR1.GND, Q2.E
  N3: U2.VIN, Q1.C
  N4: U2.GPIO17, Q2.B
  N5: R1.Pin_0, Q2.C
  N6: R1.Pin_1, Q1.E

custom parts:
  ESP32S-HiLetgo: HiLetgo ESP-WROOM-32 ESP32 ESP-32S Development Board 2.4GHz Dual-Mode WiFi + Bluetooth Dual Cores Microcontroller The ESP32 integrated with Antenna switches, RF Balun, power amplifiers, low-noise amplifiers, filters, and management modules, and the entire solution occupies the least area of PCB. 2.4 GHz Wi-Fi plus Bluetooth dual-mode chip, with TSMC Ultra-low power consumption 40nm technology,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
